# Fritzing sketch circuit (saved by Fritzing 0.9.3b)
circuit board: 6.5cm x 5.5cm
breadboards: 1

parts:
  U3 = POT [package=alps_pot]
  VCC1 = Battery block 9V
  R1 = Resistor [tolerance=±5% resistance=470 package=THT]
  LED2 = RGB LED - (4 legs) [package="5 mm [THT]"]
  R3 = Resistor [tolerance=±5% resistance=100 package=THT]
  R2 = Resistor [tolerance=±5% resistance=150 package=THT]
  R4 = Resistor [tolerance=±5% resistance=100 package=THT]
  U1 = POT [package=alps_pot]
  U2 = POT [package=alps_pot]
  LED1 = LED - 5mm [color="White (4500K)" package="5 mm [THT]"]
  R5 = Resistor [tolerance=±5% resistance=10k package=THT]
  R6 = Resistor [tolerance=±5% resistance=1k package=THT]
  IC1 = LM324 [chip_label=LM324 package="DIP (Dual Inline) [THT]"]
  IC2 = LM324 [chip_label=LM324 package="DIP (Dual Inline) [THT]"]

nets:
  N1: U3.E, VCC1.+, U1.E, U2.E, R5.Pin_0, IC1.V+, IC2.V+
  N2: U3.S, R4.Pin_1
  GND: U3.A, VCC1.-, R1.Pin_1, U1.A, U2.A, R6.Pin_1, IC1.GND, IC2.GND
  N3: R1.Pin_0, LED1.cathode
  N4: LED2.red_cathode, R2.Pin_0, IC2.Input3+
  N5: LED2.common_anode, IC1.Output2
  N6: LED2.green_cathode, R3.Pin_0, IC2.Input1+
  N7: LED2.blue_cathode, R4.Pin_0, IC2.Input2+
  N8: R3.Pin_1, U2.S
  N9: R2.Pin_1, U1.S
  N10: LED1.anode, IC1.Output1
  N11: R5.Pin_1, R6.Pin_0, IC1.Input1+, IC1.Input2-, IC2.Input1-, IC2.Input2-, IC2.Input3-, IC2.Input4-
  N12: IC1.Input1-, IC1.Input2+, IC2.Output4
  N13: IC2.Output1, IC2.Output2, IC2.Output3, IC2.Input4+

custom parts:
  LM324: LM324 Quad OpAmp
